// Logisim project 7segment.circ as structural Verilog: 7 circuits, main circuit Examples
module Examples (
  input  [7:0] in_1,
  input  [7:0] in_2,
  input  [7:0] in_3,
  input  [7:0] in_4,
  input  [7:0] in_5
);

  wire blockbottom_1_out_5, blockbottom_1_out_6, blockbottom_1_out_7, blockbottom_1_out_8,
       blockbottom_1_out_9, blockbottom_1_out_10, blockbottom_1_out_11, blockbottom_1_out_12,
       blockbottom_1_out_13, blockbottom_1_out_14, blockbottom_1_out_15, blockbottom_1_out_16,
       blockbottom_1_out_17, blockbottom_1_out_18, blockbottom_1_out_19, blockbottom_1_out_20,
       blocktop_1_out_5, blocktop_1_out_6, blocktop_1_out_7, blocktop_1_out_8, blocktop_1_out_9,
       blocktop_1_out_10, blocktop_1_out_11, blocktop_1_out_12, blocktop_1_out_13, blocktop_1_out_14,
       blocktop_1_out_15, blocktop_1_out_16, blocktop_1_out_17, blocktop_1_out_18, blocktop_1_out_19,
       blocktop_1_out_20, converterbottom_1_out_2, converterbottom_1_out_3, converterbottom_1_out_4,
       converterbottom_1_out_5, convertertop_1_out_2, convertertop_1_out_3, convertertop_1_out_4,
       convertertop_1_out_5;
  wire [7:0] blackbox_1_p1, blackbox_1_p2, blackbox_1_p3, blackbox_1_p4, blackbox_1_p6, blackbox_1_p7,
       blackbox_1_p8, blackbox_1_p9;

  ConverterTop convertertop_1 (
    .in_1(in_1), .out_2(convertertop_1_out_2), .out_3(convertertop_1_out_3), .out_4(convertertop_1_out_4),
    .out_5(convertertop_1_out_5));
  _7_Segment_Display u_7_segment_display_1 (
    .g(convertertop_1_out_2), .f(convertertop_1_out_3), .a(convertertop_1_out_4), .b(convertertop_1_out_5),
    .e(converterbottom_1_out_2), .d(converterbottom_1_out_3), .c(converterbottom_1_out_4),
    .dp(converterbottom_1_out_5));
  ConverterBottom converterbottom_1 (
    .in_1(in_1), .out_2(converterbottom_1_out_2), .out_3(converterbottom_1_out_3),
    .out_4(converterbottom_1_out_4), .out_5(converterbottom_1_out_5));
  _7_Segment_Display u_7_segment_display_2 (
    .g(blocktop_1_out_5), .f(blocktop_1_out_13), .a(blocktop_1_out_14), .b(blocktop_1_out_6),
    .e(blockbottom_1_out_13), .d(blockbottom_1_out_5), .c(blockbottom_1_out_6), .dp(blockbottom_1_out_14));
  BlockBottom blockbottom_1 (
    .out_13(blockbottom_1_out_13), .out_5(blockbottom_1_out_5), .out_6(blockbottom_1_out_6),
    .out_14(blockbottom_1_out_14), .out_15(blockbottom_1_out_15), .out_7(blockbottom_1_out_7),
    .out_8(blockbottom_1_out_8), .out_16(blockbottom_1_out_16), .out_17(blockbottom_1_out_17),
    .out_9(blockbottom_1_out_9), .out_10(blockbottom_1_out_10), .out_18(blockbottom_1_out_18),
    .out_19(blockbottom_1_out_19), .out_11(blockbottom_1_out_11), .out_12(blockbottom_1_out_12),
    .out_20(blockbottom_1_out_20), .in_1(blackbox_1_p3), .in_2(blackbox_1_p4), .in_3(blackbox_1_p6),
    .in_4(blackbox_1_p7));
  BlockTop blocktop_1 (
    .in_1(blackbox_1_p1), .in_2(blackbox_1_p2), .in_3(blackbox_1_p9), .in_4(blackbox_1_p8),
    .out_5(blocktop_1_out_5), .out_13(blocktop_1_out_13), .out_14(blocktop_1_out_14),
    .out_6(blocktop_1_out_6), .out_7(blocktop_1_out_7), .out_15(blocktop_1_out_15),
    .out_16(blocktop_1_out_16), .out_8(blocktop_1_out_8), .out_9(blocktop_1_out_9),
    .out_17(blocktop_1_out_17), .out_18(blocktop_1_out_18), .out_10(blocktop_1_out_10),
    .out_11(blocktop_1_out_11), .out_19(blocktop_1_out_19), .out_20(blocktop_1_out_20),
    .out_12(blocktop_1_out_12));
  _7_Segment_Display u_7_segment_display_3 (
    .g(blocktop_1_out_9), .f(blocktop_1_out_17), .a(blocktop_1_out_18), .b(blocktop_1_out_10),
    .e(blockbottom_1_out_17), .d(blockbottom_1_out_9), .c(blockbottom_1_out_10), .dp(blockbottom_1_out_18));
  _7_Segment_Display u_7_segment_display_4 (
    .g(blocktop_1_out_7), .f(blocktop_1_out_15), .a(blocktop_1_out_16), .b(blocktop_1_out_8),
    .e(blockbottom_1_out_15), .d(blockbottom_1_out_7), .c(blockbottom_1_out_8), .dp(blockbottom_1_out_16));
  _7_Segment_Display u_7_segment_display_5 (
    .g(blocktop_1_out_11), .f(blocktop_1_out_19), .a(blocktop_1_out_20), .b(blocktop_1_out_12),
    .e(blockbottom_1_out_19), .d(blockbottom_1_out_11), .c(blockbottom_1_out_12), .dp(blockbottom_1_out_20));
  // blackbox blackbox_1: pin names not known; wires that end beside it: blackbox_1_p1, blackbox_1_p2, blackbox_1_p3, blackbox_1_p4, {in_2, in_3, in_4, in_5}, blackbox_1_p6, blackbox_1_p7, blackbox_1_p8, blackbox_1_p9

  // Notes on the sheet:
  //   ConverterTop
  //   ConverterBottom
  //   Displayed Value
  //   Seven Segment Display
  //   DISP[3]
  //   DISP[1]
  //   DISP[2]
  //   DISP[2]
  //   DISP[0]
  //   Your Display Logic
  //   BlockTop
  //   BlockBottom
endmodule

module Converter (
  input  [7:0] in_1,
  output out_2,
  output out_3,
  output out_4,
  output out_5,
  output out_6,
  output out_7,
  output out_8,
  output out_9
);

  wire and_1_out, or_1_out;
  wire [7:0] multiplexer_1_out, multiplexer_2_out;

  Multiplexer #(.select(4), .width(8)) multiplexer_1 (
    .in0(8'h77), .in1(8'h41), .in2(8'h3b), .in3(8'h6b), .in4(8'h4d), .in5(8'h6e), .in6(8'h7e), .in7(8'h43),
    .in8(8'h7f), .in9(8'h6f), .in10(8'h5f), .in11(8'h7c), .in12(8'h36), .in13(8'h79), .in14(8'h3e),
    .in15(8'h1e), .out(multiplexer_1_out), .sel(in_1[3:0]));
  or or_1 (or_1_out, in_1[4], in_1[5], in_1[6], in_1[7]);
  Multiplexer #(.select(1), .width(8)) multiplexer_2 (
    .in0(multiplexer_1_out), .in1(8'h9b), .out(multiplexer_2_out), .sel(or_1_out));
  and and_1 (and_1_out, in_1[0], in_1[1], in_1[2], in_1[3], in_1[4], in_1[5], in_1[6], in_1[7]);
  Multiplexer #(.select(1), .width(8)) multiplexer_3 (
    .in0(multiplexer_2_out), .in1({8{1'b0}}), .out({out_9, out_8, out_7, out_6, out_2, out_3, out_4, out_5}),
    .sel(and_1_out));

  // Notes on the sheet:
  //   0
  //   1
  //   2
  //   3
  //   4
  //   5
  //   6
  //   7
  //   8
  //   9
  //   a
  //   b
  //   c
  //   d
  //   e
  //   f
  //   ?
endmodule

module ConverterTop (
  input  [7:0] in_1,
  output out_2,
  output out_3,
  output out_4,
  output out_5
);

  wire and_1_out, or_1_out;
  wire [7:0] multiplexer_1_out, multiplexer_2_out;
  wire [7:4] multiplexer_3_out;

  Multiplexer #(.select(4), .width(8)) multiplexer_1 (
    .in0(8'h77), .in1(8'h41), .in2(8'h3b), .in3(8'h6b), .in4(8'h4d), .in5(8'h6e), .in6(8'h7e), .in7(8'h43),
    .in8(8'h7f), .in9(8'h6f), .in10(8'h5f), .in11(8'h7c), .in12(8'h36), .in13(8'h79), .in14(8'h3e),
    .in15(8'h1e), .out(multiplexer_1_out), .sel(in_1[3:0]));
  or or_1 (or_1_out, in_1[4], in_1[5], in_1[6], in_1[7]);
  Multiplexer #(.select(1), .width(8)) multiplexer_2 (
    .in0(multiplexer_1_out), .in1(8'h9b), .out(multiplexer_2_out), .sel(or_1_out));
  and and_1 (and_1_out, in_1[0], in_1[1], in_1[2], in_1[3], in_1[4], in_1[5], in_1[6], in_1[7]);
  Multiplexer #(.select(1), .width(8)) multiplexer_3 (
    .in0(multiplexer_2_out), .in1({8{1'b0}}), .out({multiplexer_3_out, out_2, out_3, out_4, out_5}),
    .sel(and_1_out));

  // Notes on the sheet:
  //   0
  //   1
  //   2
  //   3
  //   4
  //   5
  //   6
  //   7
  //   8
  //   9
  //   a
  //   b
  //   c
  //   d
  //   e
  //   f
  //   ?
endmodule

module ConverterBottom (
  input  [7:0] in_1,
  output out_2,
  output out_3,
  output out_4,
  output out_5
);

  wire and_1_out, or_1_out;
  wire [3:0] multiplexer_3_out;
  wire [7:0] multiplexer_1_out, multiplexer_2_out;

  Multiplexer #(.select(4), .width(8)) multiplexer_1 (
    .in0(8'h77), .in1(8'h41), .in2(8'h3b), .in3(8'h6b), .in4(8'h4d), .in5(8'h6e), .in6(8'h7e), .in7(8'h43),
    .in8(8'h7f), .in9(8'h6f), .in10(8'h5f), .in11(8'h7c), .in12(8'h36), .in13(8'h79), .in14(8'h3e),
    .in15(8'h1e), .out(multiplexer_1_out), .sel(in_1[3:0]));
  or or_1 (or_1_out, in_1[4], in_1[5], in_1[6], in_1[7]);
  Multiplexer #(.select(1), .width(8)) multiplexer_2 (
    .in0(multiplexer_1_out), .in1(8'h9b), .out(multiplexer_2_out), .sel(or_1_out));
  and and_1 (and_1_out, in_1[0], in_1[1], in_1[2], in_1[3], in_1[4], in_1[5], in_1[6], in_1[7]);
  Multiplexer #(.select(1), .width(8)) multiplexer_3 (
    .in0(multiplexer_2_out), .in1({8{1'b0}}), .out({out_5, out_4, out_3, out_2, multiplexer_3_out}),
    .sel(and_1_out));

  // Notes on the sheet:
  //   0
  //   1
  //   2
  //   3
  //   4
  //   5
  //   6
  //   7
  //   8
  //   9
  //   a
  //   b
  //   c
  //   d
  //   e
  //   f
  //   ?
endmodule

module blackbox (
  input  Clock,
  input  [7:0] Instruction,
  input  [7:0] Data_In,
  input  Clear,
  output [7:0] out_5,
  output [7:0] out_6,
  output [7:0] out_7,
  output [7:0] out_8,
  output [7:0] out_9,
  output [7:0] out_10,
  output [7:0] out_11,
  output [7:0] out_12
);

  wire and_1_out, demultiplexer_2_out0, demultiplexer_2_out1, demultiplexer_2_out2, demultiplexer_2_out3,
       not_1_out, not_2_out, not_3_out;
  wire [7:0] demultiplexer_1_out0, demultiplexer_1_out1, demultiplexer_1_out2, demultiplexer_1_out3;

  Register #(.width(8)) register_1 (
    .D(demultiplexer_1_out0), .Q(out_6), .clk(demultiplexer_2_out0), .clr(Clear));  // open: en
  Register #(.width(8)) register_2 (
    .D(demultiplexer_1_out1), .Q(out_10), .clk(demultiplexer_2_out1), .clr(Clear));  // open: en
  Register #(.width(8)) register_3 (
    .D(demultiplexer_1_out2), .Q(out_9), .clk(demultiplexer_2_out2), .clr(Clear));  // open: en
  Register #(.width(8)) register_4 (
    .D(demultiplexer_1_out3), .Q(out_5), .clk(demultiplexer_2_out3), .clr(Clear));  // open: en
  Demultiplexer #(.select(2), .width(8), .tristate("false")) demultiplexer_1 (
    .out0(demultiplexer_1_out0), .out1(demultiplexer_1_out1), .out2(demultiplexer_1_out2),
    .out3(demultiplexer_1_out3), .in(Data_In), .sel(Instruction[1:0]));
  Demultiplexer #(.select(2), .width(1), .tristate("false")) demultiplexer_2 (
    .out0(demultiplexer_2_out0), .out1(demultiplexer_2_out1), .out2(demultiplexer_2_out2),
    .out3(demultiplexer_2_out3), .in(and_1_out), .sel(Instruction[1:0]));
  and and_1 (and_1_out, not_1_out, not_1_out, not_2_out, not_3_out, Instruction[5]);
  not not_1 (not_1_out, Clock);
  not not_2 (not_2_out, Instruction[7]);
  not not_3 (not_3_out, Instruction[6]);

  assign out_7 = out_5;
  assign out_8 = out_6;
  assign out_11 = out_9;
  assign out_12 = out_10;
endmodule

module BlockTop (
  input  [7:0] in_1,
  input  [7:0] in_2,
  input  [7:0] in_3,
  input  [7:0] in_4,
  output out_5,
  output out_6,
  output out_7,
  output out_8,
  output out_9,
  output out_10,
  output out_11,
  output out_12,
  output out_13,
  output out_14,
  output out_15,
  output out_16,
  output out_17,
  output out_18,
  output out_19,
  output out_20
);

  ConverterTop convertertop_1 (.in_1(in_1), .out_2(out_5), .out_3(out_13), .out_4(out_14), .out_5(out_6));
  ConverterTop convertertop_2 (.in_1(in_2), .out_2(out_7), .out_3(out_15), .out_4(out_16), .out_5(out_8));
  ConverterTop convertertop_3 (.in_1(in_3), .out_2(out_9), .out_3(out_17), .out_4(out_18), .out_5(out_10));
  ConverterTop convertertop_4 (.in_1(in_4), .out_2(out_11), .out_3(out_19), .out_4(out_20), .out_5(out_12));
endmodule

module BlockBottom (
  input  [7:0] in_1,
  input  [7:0] in_2,
  input  [7:0] in_3,
  input  [7:0] in_4,
  output out_5,
  output out_6,
  output out_7,
  output out_8,
  output out_9,
  output out_10,
  output out_11,
  output out_12,
  output out_13,
  output out_14,
  output out_15,
  output out_16,
  output out_17,
  output out_18,
  output out_19,
  output out_20
);

  ConverterBottom converterbottom_1 (.in_1(in_1), .out_2(out_13), .out_3(out_5), .out_4(out_6), .out_5(out_14));
  ConverterBottom converterbottom_2 (.in_1(in_2), .out_2(out_15), .out_3(out_7), .out_4(out_8), .out_5(out_16));
  ConverterBottom converterbottom_3 (.in_1(in_3), .out_2(out_17), .out_3(out_9), .out_4(out_10), .out_5(out_18));
  ConverterBottom converterbottom_4 (.in_1(in_4), .out_2(out_19), .out_3(out_11), .out_4(out_12), .out_5(out_20));
endmodule
