// Logisim project 8bit_ALU.circ as structural Verilog: 1 circuit, main circuit main
module main (
  input  F2,
  input  F1,
  input  F0,
  input  [7:0] A,
  input  [7:0] B,
  output Zero,
  output [7:0] Result,
  output Carry_Out,
  output Overflow
);

  wire alu_1_outc, alu_2_outc, alu_3_outc, alu_4_outc, alu_5_outc, alu_6_outc, alu_7_outc, decoder_1_out0,
       decoder_1_out1, decoder_1_out2, decoder_1_out3, decoder_1_out4, decoder_1_out5, decoder_1_out6,
       decoder_1_out7, or_1_out, or_2_out, or_3_out, or_4_out, or_5_out;
  wire [7:0] alu_1_output;

  Decoder #(.select(3), .tristate("false")) decoder_1 (
    .out0(decoder_1_out0), .out1(decoder_1_out1), .out2(decoder_1_out2), .out3(decoder_1_out3),
    .out4(decoder_1_out4), .out5(decoder_1_out5), .out6(decoder_1_out6), .out7(decoder_1_out7),
    .sel({F2, F1, F0}));
  // Probe on A
  // Probe on B
  or or_1 (or_1_out, 1'b0, decoder_1_out0, decoder_1_out1, decoder_1_out3, decoder_1_out4);
  or or_2 (or_2_out, decoder_1_out2, decoder_1_out7, 1'b0, or_1_out, 1'b0);
  or or_3 (or_3_out, 1'b0, decoder_1_out7, decoder_1_out6, or_1_out, decoder_1_out5);
  or or_4 (or_4_out, 1'b0, decoder_1_out7, 1'b0, 1'b0, decoder_1_out5);
  or or_5 (or_5_out, 1'b0, decoder_1_out7, 1'b0, 1'b0, decoder_1_out5);
  ALU alu_1 (
    .INVA(or_4_out), .A(A[0]), .ENA(or_3_out), .B(B[0]), .ENB(or_2_out), .F0(F0), .F1(F1), .F2(F2),
    .INC(or_5_out), .OUTC(alu_1_outc), .OUTPUT(alu_1_output[0]));
  ALU alu_2 (
    .INVA(or_4_out), .A(A[1]), .ENA(or_3_out), .B(B[1]), .ENB(or_2_out), .F0(F0), .F1(F1), .F2(F2),
    .INC(alu_1_outc), .OUTC(alu_2_outc), .OUTPUT(alu_1_output[1]));
  ALU alu_3 (
    .INVA(or_4_out), .A(A[2]), .ENA(or_3_out), .B(B[2]), .ENB(or_2_out), .F0(F0), .F1(F1), .F2(F2),
    .INC(alu_2_outc), .OUTC(alu_3_outc), .OUTPUT(alu_1_output[2]));
  ALU alu_4 (
    .INVA(or_4_out), .A(A[3]), .ENA(or_3_out), .B(B[3]), .ENB(or_2_out), .F0(F0), .F1(F1), .F2(F2),
    .INC(alu_3_outc), .OUTC(alu_4_outc), .OUTPUT(alu_1_output[3]));
  ALU alu_5 (
    .INVA(or_4_out), .A(A[4]), .ENA(or_3_out), .B(B[4]), .ENB(or_2_out), .F0(F0), .F1(F1), .F2(F2),
    .INC(alu_4_outc), .OUTC(alu_5_outc), .OUTPUT(alu_1_output[4]));
  ALU alu_6 (
    .INVA(or_4_out), .A(A[5]), .ENA(or_3_out), .B(B[5]), .ENB(or_2_out), .F0(F0), .F1(F1), .F2(F2),
    .INC(alu_5_outc), .OUTC(alu_6_outc), .OUTPUT(alu_1_output[5]));
  ALU alu_7 (
    .INVA(or_4_out), .A(A[6]), .ENA(or_3_out), .B(B[6]), .ENB(or_2_out), .F0(F0), .F1(F1), .F2(F2),
    .INC(alu_6_outc), .OUTC(alu_7_outc), .OUTPUT(alu_1_output[6]));
  ALU alu_8 (
    .INVA(or_4_out), .A(A[7]), .ENA(or_3_out), .B(B[7]), .ENB(or_2_out), .F0(F0), .F1(F1), .F2(F2),
    .INC(alu_7_outc), .OUTC(Carry_Out), .OUTPUT(alu_1_output[7]));
  xor xor_1 (Overflow, Carry_Out, alu_7_outc);
  shifter_main main_1 (.in_1(alu_1_output), .SLL(decoder_1_out6), .SLA(1'b0), .out_4(Result));
  // Probe on Result
  nor nor_1 (Zero, 1'b0, Result[0], Result[1], Result[2], Result[3], Result[4], Result[5], Result[6], Result[7]);

  // Notes on the sheet:
  //   ENB
  //   ENA
  //   INVA
  //   CIN
  //   Shifter
endmodule
