// Logisim project 8bit_ALU_plus.circ as structural Verilog: 1 circuit, main circuit main
module main (
  input  [7:0] A,
  input  [7:0] B,
  output [7:0] Result
);

  wire alu_1_outc, alu_2_outc, alu_3_outc, alu_4_outc, alu_5_outc, alu_6_outc, alu_7_outc, alu_8_outc,
       xor_1_out;

  // Probe on A
  // Probe on alu_8_outc
  ALU alu_1 (
    .INVA(1'b0), .A(A[0]), .ENA(1'b1), .B(B[0]), .ENB(1'b1), .F0(1'b0), .F1(1'b0), .F2(1'b1), .INC(1'b0),
    .OUTC(alu_1_outc), .OUTPUT(Result[0]));
  ALU alu_2 (
    .INVA(1'b0), .A(A[1]), .ENA(1'b1), .B(B[1]), .ENB(1'b1), .F0(1'b0), .F1(1'b0), .F2(1'b1),
    .INC(alu_1_outc), .OUTC(alu_2_outc), .OUTPUT(Result[1]));
  ALU alu_3 (
    .INVA(1'b0), .A(A[2]), .ENA(1'b1), .B(B[2]), .ENB(1'b1), .F0(1'b0), .F1(1'b0), .F2(1'b1),
    .INC(alu_2_outc), .OUTC(alu_3_outc), .OUTPUT(Result[2]));
  ALU alu_4 (
    .INVA(1'b0), .A(A[3]), .ENA(1'b1), .B(B[3]), .ENB(1'b1), .F0(1'b0), .F1(1'b0), .F2(1'b1),
    .INC(alu_3_outc), .OUTC(alu_4_outc), .OUTPUT(Result[3]));
  ALU alu_5 (
    .INVA(1'b0), .A(A[4]), .ENA(1'b1), .B(B[4]), .ENB(1'b1), .F0(1'b0), .F1(1'b0), .F2(1'b1),
    .INC(alu_4_outc), .OUTC(alu_5_outc), .OUTPUT(Result[4]));
  ALU alu_6 (
    .INVA(1'b0), .A(A[5]), .ENA(1'b1), .B(B[5]), .ENB(1'b1), .F0(1'b0), .F1(1'b0), .F2(1'b1),
    .INC(alu_5_outc), .OUTC(alu_6_outc), .OUTPUT(Result[5]));
  ALU alu_7 (
    .INVA(1'b0), .A(A[6]), .ENA(1'b1), .B(B[6]), .ENB(1'b1), .F0(1'b0), .F1(1'b0), .F2(1'b1),
    .INC(alu_6_outc), .OUTC(alu_7_outc), .OUTPUT(Result[6]));
  ALU alu_8 (
    .INVA(1'b0), .A(A[7]), .ENA(1'b1), .B(B[7]), .ENB(1'b1), .F0(1'b0), .F1(1'b0), .F2(1'b1),
    .INC(alu_7_outc), .OUTC(alu_8_outc), .OUTPUT(Result[7]));
  xor xor_1 (xor_1_out, alu_8_outc, alu_7_outc);
  // Probe on xor_1_out
endmodule
