// Logisim project ALU.circ as structural Verilog: 1 circuit, main circuit ALU
module ALU (
  input  INC,
  input  INVA,
  input  A,
  input  ENA,
  input  B,
  input  ENB,
  input  F0,
  input  F1,
  input  F2,
  output OUTPUT,
  output OUTC
);

  wire and_1_out, and_2_out, and_3_out, and_4_out, and_5_out, and_6_out, and_7_out, and_8_out, and_9_out,
       and_10_out, decoder_1_out0, decoder_1_out1, decoder_1_out2, decoder_1_out3, decoder_1_out4,
       decoder_1_out5, decoder_1_out6, decoder_1_out7, not_1_out, or_1_out, or_2_out, or_3_out, xor_1_out,
       xor_2_out, xor_3_out, xor_4_out;

  and and_1 (and_1_out, A, ENA);
  and and_2 (and_2_out, B, ENB);
  Decoder #(.select(3), .tristate("false")) decoder_1 (
    .out0(decoder_1_out0), .out1(decoder_1_out1), .out2(decoder_1_out2), .out3(decoder_1_out3),
    .out4(decoder_1_out4), .out5(decoder_1_out5), .out6(decoder_1_out6), .out7(decoder_1_out7),
    .sel({F2, F1, F0}));
  xor xor_1 (xor_1_out, INVA, and_1_out);
  and and_3 (and_3_out, xor_1_out, and_2_out);
  or or_1 (or_1_out, xor_1_out, and_2_out);
  not not_1 (not_1_out, and_2_out);
  xor xor_2 (xor_2_out, xor_1_out, and_2_out);
  or or_2 (or_2_out, decoder_1_out4, decoder_1_out5, decoder_1_out7, 1'b0, 1'b0);
  and and_4 (and_4_out, or_2_out, and_2_out, xor_1_out);
  and and_5 (and_5_out, and_3_out, decoder_1_out0);
  or or_3 (or_3_out, decoder_1_out1, decoder_1_out6);
  and and_6 (and_6_out, not_1_out, decoder_1_out2);
  and and_7 (and_7_out, xor_2_out, decoder_1_out3);
  xor xor_3 (xor_3_out, and_2_out, xor_1_out);
  and and_8 (and_8_out, or_2_out, xor_3_out, INC);
  or or_4 (OUTC, and_4_out, and_8_out);
  and and_9 (and_9_out, or_1_out, or_3_out);
  xor xor_4 (xor_4_out, INC, xor_3_out);
  and and_10 (and_10_out, xor_4_out, or_2_out);
  or or_5 (OUTPUT, and_5_out, and_9_out, and_6_out, and_7_out, and_10_out);

  // Notes on the sheet:
  //   Not B
  //   A XOR B
  //   AB
  //   A or B
  //   A plus B
endmodule
