// Logisim project alu_control.circ as structural Verilog: 1 circuit, main circuit main
module main (
  input  [7:0] in_1,
  input  [1:0] in_2,
  output out_3,
  output out_4,
  output out_5
);

  wire and_1_out, and_2_out, not_1_out, not_2_out, not_3_out, not_4_out;
  wire [2:0] controlled_buffer_1_out;

  // Probe on in_1[4:3]
  not not_1 (not_1_out, in_1[5]);
  not not_2 (not_2_out, in_1[6]);
  not not_3 (not_3_out, in_1[7]);
  not not_4 (not_4_out, in_1[7]);
  and and_1 (and_1_out, not_1_out, not_2_out, not_3_out);
  and and_2 (and_2_out, in_1[5], in_1[6], not_4_out);
  assign controlled_buffer_1_out = and_1_out ? in_1[2:0] : 3'bz;  // Controlled_Buffer controlled_buffer_1
  assign controlled_buffer_1_out = and_2_out ? 3'b001 : 3'bz;  // Controlled_Buffer controlled_buffer_2
  Multiplexer #(.select(2), .width(3)) multiplexer_1 (
    .in0(3'b100), .in1(3'b111), .in2(controlled_buffer_1_out), .in3(3'b000), .out({out_3, out_4, out_5}),
    .sel(in_2));
endmodule
