// Logisim project control.circ as structural Verilog: 1 circuit, main circuit main
module main (
  input  [7:0] Instruction,
  output Reg_Dst,
  output Reg_Write,
  output ALU_Src,
  output MemWrite,
  output MemRead,
  output MemtoReg,
  output [1:0] ALUOp,
  output Branch,
  output Jump
);

  wire decoder_1_out0, decoder_1_out1, decoder_1_out2, decoder_1_out3, decoder_1_out4, decoder_1_out5,
       decoder_1_out6, decoder_1_out7, not_1_out, not_2_out, not_3_out, not_4_out, not_5_out, not_6_out,
       not_7_out, not_8_out, not_9_out, not_10_out, not_11_out, not_12_out, not_13_out, not_14_out,
       not_15_out, not_16_out, not_17_out, not_18_out, not_19_out, not_20_out, not_21_out, not_22_out,
       not_23_out, not_24_out, not_25_out, not_26_out, not_27_out, not_28_out, or_1_out, or_2_out, or_3_out,
       or_4_out;

  // Probe on Instruction[4:0]
  Decoder #(.select(3), .tristate("false")) decoder_1 (
    .out0(decoder_1_out0), .out1(decoder_1_out1), .out2(decoder_1_out2), .out3(decoder_1_out3),
    .out4(decoder_1_out4), .out5(decoder_1_out5), .out6(decoder_1_out6), .out7(decoder_1_out7),
    .sel(Instruction[7:5]));
  not not_1 (not_1_out, decoder_1_out5);
  not not_2 (not_2_out, decoder_1_out6);
  not not_3 (not_3_out, decoder_1_out7);
  not not_4 (not_4_out, decoder_1_out0);
  not not_5 (not_5_out, decoder_1_out7);
  not not_6 (not_6_out, decoder_1_out0);
  not not_7 (not_7_out, decoder_1_out4);
  not not_8 (not_8_out, decoder_1_out6);
  not not_9 (not_9_out, decoder_1_out7);
  not not_10 (not_10_out, decoder_1_out0);
  not not_11 (not_11_out, decoder_1_out5);
  not not_12 (not_12_out, decoder_1_out6);
  not not_13 (not_13_out, decoder_1_out7);
  not not_14 (not_14_out, decoder_1_out0);
  not not_15 (not_15_out, decoder_1_out0);
  not not_16 (not_16_out, decoder_1_out3);
  not not_17 (not_17_out, decoder_1_out4);
  not not_18 (not_18_out, decoder_1_out5);
  not not_19 (not_19_out, decoder_1_out4);
  not not_20 (not_20_out, decoder_1_out5);
  not not_21 (not_21_out, decoder_1_out7);
  not not_22 (not_22_out, decoder_1_out0);
  not not_23 (not_23_out, decoder_1_out4);
  not not_24 (not_24_out, decoder_1_out5);
  not not_25 (not_25_out, decoder_1_out0);
  not not_26 (not_26_out, decoder_1_out4);
  not not_27 (not_27_out, decoder_1_out5);
  not not_28 (not_28_out, decoder_1_out7);
  or or_1 (or_1_out, decoder_1_out0, decoder_1_out1, decoder_1_out2, decoder_1_out3, decoder_1_out4);
  or or_2 (or_2_out, decoder_1_out0, decoder_1_out1, decoder_1_out2, decoder_1_out3, decoder_1_out4);
  or or_3 (or_3_out, decoder_1_out2, decoder_1_out3, decoder_1_out4, 1'b0, decoder_1_out5);
  and and_1 (MemWrite, not_6_out, 1'b1, 1'b1, 1'b1, 1'b1, not_7_out, decoder_1_out5, not_8_out, not_9_out);
  and and_2 (MemRead, not_10_out, 1'b1, 1'b1, 1'b1, 1'b1, decoder_1_out4, not_11_out, not_12_out, not_13_out);
  and and_3 (MemtoReg, not_14_out, 1'b1, 1'b1, 1'b1, decoder_1_out4, 1'b1, 1'b1, 1'b1, 1'b1);
  or or_4 (or_4_out, decoder_1_out0, 1'b0, 1'b0, 1'b0, decoder_1_out3);
  and and_4 (Branch, not_22_out, 1'b1, 1'b1, 1'b1, 1'b1, not_23_out, not_24_out, 1'b1, decoder_1_out7);
  and and_5 (Jump, not_25_out, 1'b1, 1'b1, 1'b1, 1'b1, not_26_out, not_27_out, decoder_1_out6, not_28_out);
  and and_6 (Reg_Dst, 1'b1, 1'b1, or_1_out, 1'b1, 1'b1, 1'b1, 1'b1, 1'b1);
  and and_7 (ALUOp[0], not_15_out, 1'b1, 1'b1, 1'b1, not_16_out, not_17_out, not_18_out, 1'b1, decoder_1_out7);
  and and_8 (ALUOp[1], 1'b1, 1'b1, or_4_out, 1'b1, 1'b1, not_19_out, not_20_out, 1'b1, not_21_out);
  and and_9 (Reg_Write, 1'b1, 1'b1, or_2_out, 1'b1, 1'b1, 1'b1, not_1_out, not_2_out, not_3_out);
  and and_10 (ALU_Src, not_4_out, 1'b1, 1'b1, 1'b1, or_3_out, 1'b1, 1'b1, 1'b1, not_5_out);
endmodule
