// Logisim project data_memory.circ as structural Verilog: 1 circuit, main circuit main
module main (
  input  [7:0] Address,
  input  [7:0] Data_In,
  input  Clock,
  input  Clear,
  input  MemWrite,
  input  MemRead,
  output [7:0] Data_Out
);

  wire not_1_out, not_2_out, or_1_out, xnor_1_out;

  not not_1 (not_1_out, Clock);
  assign Data_Out = not_2_out ? Data_In : 8'bz;  // Controlled_Buffer controlled_buffer_1
  not not_2 (not_2_out, or_1_out);
  RAM #(.addrWidth(8), .dataWidth(8)) ram_1 (
    .addr(Address), .data(Data_Out), .clk(not_1_out), .ld(or_1_out), .clr(Clear));  // open: sel
  or or_1 (or_1_out, xnor_1_out, MemRead);
  xnor xnor_1 (xnor_1_out, MemWrite, MemRead);
endmodule
