// Logisim project miniMips.circ as structural Verilog: 1 circuit, main circuit main
module main (
);

  wire and_1_out, blockbottom_1_out_5, blockbottom_1_out_6, blockbottom_1_out_7, blockbottom_1_out_8,
       blockbottom_1_out_9, blockbottom_1_out_10, blockbottom_1_out_11, blockbottom_1_out_12,
       blockbottom_1_out_13, blockbottom_1_out_14, blockbottom_1_out_15, blockbottom_1_out_16,
       blockbottom_1_out_17, blockbottom_1_out_18, blockbottom_1_out_19, blockbottom_1_out_20,
       blocktop_1_out_5, blocktop_1_out_6, blocktop_1_out_7, blocktop_1_out_8, blocktop_1_out_9,
       blocktop_1_out_10, blocktop_1_out_11, blocktop_1_out_12, blocktop_1_out_13, blocktop_1_out_14,
       blocktop_1_out_15, blocktop_1_out_16, blocktop_1_out_17, blocktop_1_out_18, blocktop_1_out_19,
       blocktop_1_out_20, Clock_out, main_1_alu_src, main_1_branch, main_1_jump, main_1_memread,
       main_1_memtoreg, main_1_memwrite, main_1_reg_dst, main_1_reg_write, main_6_out_3, main_6_out_4,
       main_6_out_5, main_7_zero, Reset_out;
  wire [1:0] main_1_aluop;
  wire [7:0] blackbox_1_out_5, blackbox_1_out_6, blackbox_1_out_7, blackbox_1_out_8, blackbox_1_out_9,
       blackbox_1_out_10, blackbox_1_out_11, blackbox_1_out_12, main_2_result, main_3_signed_offset_i,
       main_4_rd, main_4_rx, main_5_result, main_7_result, main_8_data_out, multiplexer_1_out,
       multiplexer_2_out, multiplexer_3_out, multiplexer_4_out, register_1_q, rom_1_data;

  control_main main_1 (
    .Instruction(rom_1_data), .Reg_Dst(main_1_reg_dst), .Reg_Write(main_1_reg_write),
    .ALU_Src(main_1_alu_src), .MemWrite(main_1_memwrite), .MemRead(main_1_memread),
    .MemtoReg(main_1_memtoreg), .ALUOp(main_1_aluop), .Branch(main_1_branch), .Jump(main_1_jump));
  _7_Segment_Display u_7_segment_display_1 (
    .g(blocktop_1_out_7), .f(blocktop_1_out_15), .a(blocktop_1_out_16), .b(blocktop_1_out_8),
    .e(blockbottom_1_out_15), .d(blockbottom_1_out_7), .c(blockbottom_1_out_8), .dp(blockbottom_1_out_16));
  _7_Segment_Display u_7_segment_display_2 (
    .g(blocktop_1_out_5), .f(blocktop_1_out_13), .a(blocktop_1_out_14), .b(blocktop_1_out_6),
    .e(blockbottom_1_out_13), .d(blockbottom_1_out_5), .c(blockbottom_1_out_6), .dp(blockbottom_1_out_14));
  BlockBottom blockbottom_1 (
    .out_13(blockbottom_1_out_13), .out_5(blockbottom_1_out_5), .out_6(blockbottom_1_out_6),
    .out_14(blockbottom_1_out_14), .out_15(blockbottom_1_out_15), .out_7(blockbottom_1_out_7),
    .out_8(blockbottom_1_out_8), .out_16(blockbottom_1_out_16), .out_17(blockbottom_1_out_17),
    .out_9(blockbottom_1_out_9), .out_10(blockbottom_1_out_10), .out_18(blockbottom_1_out_18),
    .out_19(blockbottom_1_out_19), .out_11(blockbottom_1_out_11), .out_12(blockbottom_1_out_12),
    .out_20(blockbottom_1_out_20), .in_1(blackbox_1_out_5), .in_2(blackbox_1_out_9),
    .in_3(blackbox_1_out_10), .in_4(blackbox_1_out_6));
  Register #(.width(8)) register_1 (
    .D(multiplexer_2_out), .Q(register_1_q), .clk(Clock_out), .clr(Reset_out));  // open: en
  BlockTop blocktop_1 (
    .in_1(blackbox_1_out_7), .in_2(blackbox_1_out_11), .in_3(blackbox_1_out_12), .in_4(blackbox_1_out_8),
    .out_5(blocktop_1_out_5), .out_13(blocktop_1_out_13), .out_14(blocktop_1_out_14),
    .out_6(blocktop_1_out_6), .out_7(blocktop_1_out_7), .out_15(blocktop_1_out_15),
    .out_16(blocktop_1_out_16), .out_8(blocktop_1_out_8), .out_9(blocktop_1_out_9),
    .out_17(blocktop_1_out_17), .out_18(blocktop_1_out_18), .out_10(blocktop_1_out_10),
    .out_11(blocktop_1_out_11), .out_19(blocktop_1_out_19), .out_20(blocktop_1_out_20),
    .out_12(blocktop_1_out_12));
  _7_Segment_Display u_7_segment_display_3 (
    .g(blocktop_1_out_11), .f(blocktop_1_out_19), .a(blocktop_1_out_20), .b(blocktop_1_out_12),
    .e(blockbottom_1_out_19), .d(blockbottom_1_out_11), .c(blockbottom_1_out_12), .dp(blockbottom_1_out_20));
  _7_Segment_Display u_7_segment_display_4 (
    .g(blocktop_1_out_9), .f(blocktop_1_out_17), .a(blocktop_1_out_18), .b(blocktop_1_out_10),
    .e(blockbottom_1_out_17), .d(blockbottom_1_out_9), .c(blockbottom_1_out_10), .dp(blockbottom_1_out_18));
  blackbox blackbox_1 (
    .out_7(blackbox_1_out_7), .out_11(blackbox_1_out_11), .Instruction(rom_1_data), .Data_In(main_4_rd),
    .out_5(blackbox_1_out_5), .out_9(blackbox_1_out_9), .out_10(blackbox_1_out_10), .out_6(blackbox_1_out_6),
    .Clock(Clock_out), .Clear(Reset_out), .out_8(blackbox_1_out_8), .out_12(blackbox_1_out_12));
  _8bit_ALU_plus_1_main main_2 (.A(register_1_q), .Result(main_2_result));
  Button Clock (.out(Clock_out));
  Button Reset (.out(Reset_out));
  ROM #(.addrWidth(8), .dataWidth(8)) rom_1 (.addr(register_1_q), .data(rom_1_data));  // open: sel
  sign_extend_main main_3 (
    .Instruction(rom_1_data), .PC_instruction(main_2_result), .Signed_Offset_I(main_3_signed_offset_i));
  register_file2_main main_4 (
    .Instruction(rom_1_data), .Write_Data(multiplexer_4_out), .Clock(Clock_out), .Clear(Reset_out),
    .Reg_Dst(main_1_reg_dst), .Reg_Write(main_1_reg_write), .rd(main_4_rd), .rx(main_4_rx));
  _8bit_ALU_plus_main main_5 (.A(main_2_result), .B(main_3_signed_offset_i), .Result(main_5_result));
  Multiplexer #(.select(1), .width(8)) multiplexer_1 (
    .in0(main_4_rx), .in1(main_3_signed_offset_i), .out(multiplexer_1_out), .sel(main_1_alu_src));
  alu_control_main main_6 (
    .in_1(rom_1_data), .out_3(main_6_out_3), .out_4(main_6_out_4), .out_5(main_6_out_5), .in_2(main_1_aluop));
  _8bit_ALU_main main_7 (
    .A(main_4_rd), .B(multiplexer_1_out), .F2(main_6_out_3), .F1(main_6_out_4), .F0(main_6_out_5),
    .Zero(main_7_zero), .Result(main_7_result));  // open: Carry_Out, Overflow
  and and_1 (and_1_out, main_7_zero, main_1_branch);
  Multiplexer #(.select(1), .width(8)) multiplexer_2 (
    .in0(multiplexer_3_out), .in1(main_3_signed_offset_i), .out(multiplexer_2_out), .sel(main_1_jump));
  Multiplexer #(.select(1), .width(8)) multiplexer_3 (
    .in0(main_2_result), .in1(main_5_result), .out(multiplexer_3_out), .sel(and_1_out));
  data_memory_main main_8 (
    .Address(main_7_result), .Data_In(main_4_rx), .Clock(Clock_out), .Clear(Reset_out),
    .MemWrite(main_1_memwrite), .MemRead(main_1_memread), .Data_Out(main_8_data_out));
  Multiplexer #(.select(1), .width(8)) multiplexer_4 (
    .in0(main_7_result), .in1(main_8_data_out), .out(multiplexer_4_out), .sel(main_1_memtoreg));

  // Notes on the sheet:
  //   CONTROL
  //   PC
  //   +1
  //   Sign Extend
  //   contents of rom_1 (hex, n*v repeats v):
  //   40 67 50 74 a0 b1 81 22 90 33 17 b2 82 30 40 50 ff
  //   +
  //   Rg File
  //   Ctrl
  //   ALU
  //   Mem
endmodule
