// Logisim project register_file.circ as structural Verilog: 1 circuit, main circuit main
module main (
  input  [7:0] Instruction,
  input  [7:0] Write_Data,
  input  Reg_Dst,
  input  Reg_Write,
  input  Clock,
  input  Clear,
  output [7:0] rd,
  output [7:0] rx
);

  wire and_1_out, and_2_out, and_3_out, decoder_1_out0, decoder_1_out1, decoder_1_out2, decoder_1_out3,
       decoder_1_out4, decoder_1_out5, decoder_1_out6, decoder_1_out7, decoder_2_out0, decoder_2_out1,
       multiplexer_1_out, multiplexer_2_out, multiplexer_4_out, multiplexer_5_out, not_1_out, not_2_out,
       not_3_out, or_1_out, or_2_out, or_3_out;
  wire [7:0] multiplexer_3_out, multiplexer_6_out, register_1_q, register_2_q;

  Decoder #(.select(3), .tristate("false")) decoder_1 (
    .out0(decoder_1_out0), .out1(decoder_1_out1), .out2(decoder_1_out2), .out3(decoder_1_out3),
    .out4(decoder_1_out4), .out5(decoder_1_out5), .out6(decoder_1_out6), .out7(decoder_1_out7),
    .sel(Instruction[7:5]));
  or or_1 (or_1_out, decoder_1_out7, decoder_1_out0, decoder_1_out5);
  or or_2 (or_2_out, decoder_1_out6, decoder_1_out2, decoder_1_out4, decoder_1_out5);
  or or_3 (or_3_out, decoder_1_out1, decoder_1_out3, decoder_1_out4, decoder_1_out6);
  Multiplexer #(.select(1), .width(1)) multiplexer_1 (
    .in0(Instruction[3]), .in1(Instruction[4]), .out(multiplexer_1_out), .sel(Reg_Dst));
  Decoder #(.select(1), .tristate("false")) decoder_2 (
    .out0(decoder_2_out0), .out1(decoder_2_out1), .sel(multiplexer_1_out));
  not not_1 (not_1_out, Clock);
  and and_1 (and_1_out, decoder_2_out0, Reg_Write, not_1_out);
  and and_2 (and_2_out, decoder_2_out1, Reg_Write, not_1_out);
  Register #(.width(8)) register_1 (.D(Write_Data), .Q(register_1_q), .clk(and_1_out), .clr(Clear));  // open: en
  Register #(.width(8)) register_2 (.D(Write_Data), .Q(register_2_q), .clk(and_2_out), .clr(Clear));  // open: en
  Multiplexer #(.select(1), .width(1)) multiplexer_2 (
    .in0(Instruction[4]), .in1(1'b1), .out(multiplexer_2_out), .sel(and_3_out));
  and and_3 (and_3_out, not_2_out, or_1_out);
  not not_2 (not_2_out, decoder_1_out5);
  not not_3 (not_3_out, multiplexer_2_out);
  Multiplexer #(.select(1), .width(8)) multiplexer_3 (
    .in0(register_1_q), .in1(register_2_q), .out(multiplexer_3_out), .sel(multiplexer_4_out));
  Multiplexer #(.select(1), .width(1)) multiplexer_4 (
    .in0(Instruction[4]), .in1(not_3_out), .out(multiplexer_4_out), .sel(or_1_out));
  Multiplexer #(.select(1), .width(1)) multiplexer_5 (
    .in0(Instruction[3]), .in1(multiplexer_2_out), .out(multiplexer_5_out), .sel(or_1_out));
  Multiplexer #(.select(1), .width(8)) multiplexer_6 (
    .in0(register_1_q), .in1(register_2_q), .out(multiplexer_6_out), .sel(multiplexer_5_out));
  Multiplexer #(.select(1), .width(8)) multiplexer_7 (
    .in0(multiplexer_3_out), .in1({8{1'b0}}), .out(rd), .sel(or_2_out));
  Multiplexer #(.select(1), .width(8)) multiplexer_8 (
    .in0(multiplexer_6_out), .in1({8{1'b0}}), .out(rx), .sel(or_3_out));

  // Notes on the sheet:
  //   $r0
  //   $r1
endmodule
