// Logisim project reg_file_combinational2.circ as structural Verilog: 1 circuit, main circuit main
module main (
  input  [2:0] in_1,
  input  in_2,
  input  in_3,
  output Zero_on_Top,
  output Zero_on_Bottom,
  output out_6,
  output out_7
);

  wire and_1_out, decoder_1_out0, decoder_1_out1, decoder_1_out2, decoder_1_out3, decoder_1_out4,
       decoder_1_out5, decoder_1_out6, decoder_1_out7, multiplexer_1_out, not_1_out, not_2_out, or_1_out;

  Decoder #(.select(3), .tristate("false")) decoder_1 (
    .out0(decoder_1_out0), .out1(decoder_1_out1), .out2(decoder_1_out2), .out3(decoder_1_out3),
    .out4(decoder_1_out4), .out5(decoder_1_out5), .out6(decoder_1_out6), .out7(decoder_1_out7), .sel(in_1));
  or or_1 (or_1_out, decoder_1_out7, decoder_1_out0, decoder_1_out5);
  or or_2 (Zero_on_Top, decoder_1_out6, 1'b0, decoder_1_out2, decoder_1_out4, decoder_1_out5);
  or or_3 (Zero_on_Bottom, decoder_1_out1, decoder_1_out3, 1'b0, decoder_1_out4, decoder_1_out6);
  Multiplexer #(.select(1), .width(1)) multiplexer_1 (.in0(in_2), .in1(1'b1), .out(multiplexer_1_out), .sel(and_1_out));
  and and_1 (and_1_out, not_1_out, or_1_out);
  not not_1 (not_1_out, decoder_1_out5);
  Multiplexer #(.select(1), .width(1)) multiplexer_2 (.in0(in_2), .in1(not_2_out), .out(out_6), .sel(or_1_out));
  not not_2 (not_2_out, multiplexer_1_out);
  Multiplexer #(.select(1), .width(1)) multiplexer_3 (.in0(in_3), .in1(multiplexer_1_out), .out(out_7), .sel(or_1_out));
endmodule
