// Logisim project register_file2.circ as structural Verilog: 1 circuit, main circuit main
module main (
  input  [7:0] Instruction,
  input  [7:0] Write_Data,
  input  Clock,
  input  Clear,
  input  Reg_Dst,
  input  Reg_Write,
  output [7:0] rd,
  output [7:0] rx
);

  wire and_1_out, and_2_out, decoder_1_out0, decoder_1_out1, main_1_out_6, main_1_out_7,
       main_1_zero_on_bottom, main_1_zero_on_top, multiplexer_1_out, not_1_out;
  wire [7:0] multiplexer_2_out, multiplexer_3_out, register_1_q, register_2_q;

  // Probe on Instruction[2:0]
  Multiplexer #(.select(1), .width(1)) multiplexer_1 (
    .in0(Instruction[3]), .in1(Instruction[4]), .out(multiplexer_1_out), .sel(Reg_Dst));
  Decoder #(.select(1), .tristate("false")) decoder_1 (
    .out0(decoder_1_out0), .out1(decoder_1_out1), .sel(multiplexer_1_out));
  not not_1 (not_1_out, Clock);
  and and_1 (and_1_out, decoder_1_out0, Reg_Write, not_1_out);
  and and_2 (and_2_out, decoder_1_out1, Reg_Write, not_1_out);
  Register #(.width(8)) register_1 (.D(Write_Data), .Q(register_1_q), .clk(and_1_out), .clr(Clear));  // open: en
  Register #(.width(8)) register_2 (.D(Write_Data), .Q(register_2_q), .clk(and_2_out), .clr(Clear));  // open: en
  reg_file_combinational2_main main_1 (
    .in_1(Instruction[7:5]), .in_2(Instruction[4]), .in_3(Instruction[3]), .out_6(main_1_out_6),
    .out_7(main_1_out_7), .Zero_on_Top(main_1_zero_on_top), .Zero_on_Bottom(main_1_zero_on_bottom));
  Multiplexer #(.select(1), .width(8)) multiplexer_2 (
    .in0(register_1_q), .in1(register_2_q), .out(multiplexer_2_out), .sel(main_1_out_6));
  Multiplexer #(.select(1), .width(8)) multiplexer_3 (
    .in0(register_1_q), .in1(register_2_q), .out(multiplexer_3_out), .sel(main_1_out_7));
  Multiplexer #(.select(1), .width(8)) multiplexer_4 (
    .in0(multiplexer_2_out), .in1({8{1'b0}}), .out(rd), .sel(main_1_zero_on_top));
  Multiplexer #(.select(1), .width(8)) multiplexer_5 (
    .in0(multiplexer_3_out), .in1({8{1'b0}}), .out(rx), .sel(main_1_zero_on_bottom));

  // Notes on the sheet:
  //   $r0
  //   $r1
  //   Combinational Logic
endmodule
