// Logisim project shifter.circ as structural Verilog: 1 circuit, main circuit main
module main (
  input  [7:0] in_1,
  input  SLL,
  input  SLA,
  output [7:0] out_4
);

  wire and_1_out, and_3_out, and_4_out, and_5_out, and_6_out, and_7_out, and_8_out, and_9_out, and_10_out,
       and_11_out, and_12_out, and_13_out, and_14_out, and_15_out, not_1_out, not_2_out, or_1_out;
  wire [7:0] and_2_out;

  not not_1 (not_1_out, SLL);
  or or_1 (or_1_out, SLL, SLA);
  not not_2 (not_2_out, 1'b0);
  and and_1 (and_1_out, in_1[0], not_2_out);
  and and_2 (and_2_out[0], 1'b0, in_1[1]);
  and and_3 (and_3_out, in_1[1], not_2_out);
  and and_4 (and_4_out, 1'b0, in_1[2]);
  and and_5 (and_5_out, in_1[2], not_2_out);
  and and_6 (and_6_out, 1'b0, in_1[3]);
  and and_7 (and_7_out, in_1[3], not_2_out);
  and and_8 (and_8_out, 1'b0, in_1[4]);
  and and_9 (and_9_out, in_1[4], not_2_out);
  and and_10 (and_10_out, 1'b0, in_1[5]);
  and and_11 (and_11_out, in_1[5], not_2_out);
  and and_12 (and_12_out, 1'b0, in_1[6]);
  and and_13 (and_13_out, in_1[6], not_2_out);
  and and_14 (and_14_out, 1'b0, in_1[7]);
  and and_15 (and_15_out, in_1[7], 1'b0, not_1_out);
  or or_2 (and_2_out[1], and_1_out, and_4_out);
  or or_3 (and_2_out[2], and_3_out, and_6_out);
  or or_4 (and_2_out[3], and_5_out, and_8_out);
  or or_5 (and_2_out[4], and_7_out, and_10_out);
  or or_6 (and_2_out[5], and_9_out, and_12_out);
  or or_7 (and_2_out[6], and_11_out, and_14_out);
  or or_8 (and_2_out[7], and_13_out, and_15_out);
  Multiplexer #(.select(1), .width(8)) multiplexer_1 (.in0(in_1), .in1(and_2_out), .out(out_4), .sel(or_1_out));

  // Notes on the sheet:
  //   (0 = left, 1 = right)
  //   L
  //   L
  //   R
  //   R
  //   L
  //   R
  //   L
  //   R
  //   L
  //   R
  //   L
  //   R
  //   L
  //   R
endmodule
