// Logisim project sign_extend.circ as structural Verilog: 1 circuit, main circuit main
module main (
  input  [7:0] Instruction,
  input  [7:0] PC_instruction,
  output [7:0] Signed_Offset_I
);

  wire and_1_out, and_2_out, and_3_out, and_4_out, decoder_1_out2, decoder_1_out3, decoder_1_out4,
       decoder_1_out5, decoder_1_out6, decoder_1_out7, not_1_out, not_2_out, not_3_out, not_4_out, not_5_out,
       not_6_out, not_7_out, not_8_out, not_9_out, not_10_out, not_11_out, not_12_out, or_1_out;
  wire [1:0] decoder_1_out0;

  // Probe on PC_instruction[4:0]
  Decoder #(.select(3), .tristate("false")) decoder_1 (
    .out0(decoder_1_out0[0]), .out1(decoder_1_out0[1]), .out2(decoder_1_out2), .out3(decoder_1_out3),
    .out4(decoder_1_out4), .out5(decoder_1_out5), .out6(decoder_1_out6), .out7(decoder_1_out7),
    .sel(Instruction[7:5]));
  // Probe on decoder_1_out0
  or or_1 (or_1_out, 1'b0, 1'b0, decoder_1_out3, decoder_1_out4, decoder_1_out5);
  not not_1 (not_1_out, or_1_out);
  not not_2 (not_2_out, decoder_1_out6);
  not not_3 (not_3_out, decoder_1_out7);
  not not_4 (not_4_out, decoder_1_out2);
  not not_5 (not_5_out, decoder_1_out6);
  not not_6 (not_6_out, decoder_1_out7);
  not not_7 (not_7_out, decoder_1_out2);
  not not_8 (not_8_out, or_1_out);
  not not_9 (not_9_out, decoder_1_out7);
  not not_10 (not_10_out, decoder_1_out2);
  not not_11 (not_11_out, or_1_out);
  not not_12 (not_12_out, decoder_1_out6);
  assign Signed_Offset_I = and_3_out ? {PC_instruction[7:5], Instruction[4:0]} : 8'bz;  // Controlled_Buffer controlled_buffer_1
  and and_1 (and_1_out, decoder_1_out2, not_1_out, not_2_out, not_3_out);
  and and_2 (and_2_out, not_4_out, or_1_out, not_5_out, not_6_out);
  and and_3 (and_3_out, not_7_out, not_8_out, decoder_1_out6, not_9_out);
  and and_4 (and_4_out, not_10_out, not_11_out, not_12_out, decoder_1_out7);
  assign Signed_Offset_I = and_2_out ? {4'b0000, Instruction[3:0]} : 8'bz;  // Controlled_Buffer controlled_buffer_2
  assign Signed_Offset_I = and_4_out ? {{4{Instruction[4]}}, Instruction[3:0]} : 8'bz;  // Controlled_Buffer controlled_buffer_3
  assign Signed_Offset_I = and_1_out ? {Instruction[3:0], 4'b0000} : 8'bz;  // Controlled_Buffer controlled_buffer_4
endmodule
